// Logisim project FIT1047_ws_01_circuit_2.circ as structural Verilog: 1 circuit, main circuit main
module main (
  input  in_1,
  input  in_2,
  input  in_3,
  output out_4
);

  wire or_1_out, or_2_out, or_3_out, or_4_out, or_5_out;

  or or_1 (or_1_out, in_1, in_2);
  or or_2 (or_2_out, or_1_out, or_3_out);
  or or_3 (or_3_out, in_1, in_3);
  or or_4 (or_4_out, in_2, in_3);
  or or_5 (or_5_out, or_3_out, or_4_out);
  or or_6 (out_4, or_2_out, or_5_out);
endmodule
