// Logisim project FIT1047_ws_01_circuit_3.circ as structural Verilog: 1 circuit, main circuit main
module main (
  input  in_1,
  input  in_2,
  output out_3,
  output out_4
);

  wire not_1_out, or_1_out;

  and and_1 (out_3, in_1, in_2);
  or or_1 (or_1_out, in_1, in_2);
  not not_1 (not_1_out, out_3);
  and and_2 (out_4, not_1_out, or_1_out);
endmodule
