// Logisim project workshop3-Task1B2-template.circ as structural Verilog: 1 circuit, main circuit main
module main (
  input  A,
  input  B,
  input  C,
  output D0,
  output D1
);

  wire not_1_out, not_2_out, not_3_out;

  not not_1 (not_1_out, A);
  not not_2 (not_2_out, B);
  not not_3 (not_3_out, C);
  // AND_Gate and_1 has open pins: out=D0
  // AND_Gate and_2 has open pins: out=D1

  // Notes on the sheet:
  //   3-bit Decoder
  //   ...... (add more AND gates)
endmodule
