// Logisim project workshopactivity.circ as structural Verilog: 1 circuit, main circuit main
module main (
  input  X,
  input  Z,
  input  Y,
  input  in_4,
  input  in_5,
  output F,
  output out_7
);

  wire and_1_out, and_2_out, not_1_out;

  not not_1 (not_1_out, Z);
  and and_1 (and_1_out, X, not_1_out);
  and and_2 (and_2_out, in_4, in_4);
  and and_3 (out_7, and_2_out, in_4);
  or or_1 (F, and_1_out, Y);

  assign in_5 = in_4;
endmodule
